# Fritzing sketch Schematic  Diagram (saved by Fritzing 0.9.3b)
circuit board: 8.46667cm x 5.64444cm

parts:
  LCD1 = LCD screen
  Part4 = Arduino BT
  R1 = Resistor [tolerance=±5% resistance=220 package=THT]  # not connected
  A1 = 2957N11 pressure sensor
  Adafruit_HUZZAH_ESP8266_Breakout1 = Adafruit HUZZAH ESP8266 Breakout [part_number=2471]
  wire = HX711 Weighing Sensor Module

nets (from the breadboard view):
  N1: LCD1.RS, Part4.PWM_D9
  N2: LCD1.R/W, Part4.D8
  N3: LCD1.DB4, Part4.SS/PWM_D10
  N4: LCD1.DB5, Part4.MOSI/PWM_D11
  N5: LCD1.DB6, Part4.MISO/D12
  N6: LCD1.DB7, Part4.SCK/D13
  5V: Part4.5V, wire.VCC
  GND: Part4.GND, wire.GND
  N7: Part4.A0, A1.Pin_3
  N8: Part4.D2, wire.DO/RX
  N9: Part4.PWM_D3, wire.CK/TX
  N10: Part4.3V3, Adafruit_HUZZAH_ESP8266_Breakout1.3V

custom parts:
  2957N11 pressure sensor: Monitor and control vacuum pumps, air compressors, and hydraulics. These transmitters convert both pressure and vacuum into an electrical signal that can be interpreted by receiving devices, such as remote displays, programmable logic controllers, and motor speed controls.
  HX711 Weighing Sensor Module: HX711 is a precision 24-bit analog-to-digital converter (ADC) designed for weigh scales and industrial control applications to interface directly with a bridge sensor.
